// Logisim project regfile.circ as structural Verilog: 1 circuit, main circuit main
module main (
  input  [1:0] Read_register_1,
  input  [1:0] Read_register_2,
  input  [1:0] write_register,
  input  [31:0] write_data,
  input  RegWrite,
  input  clock,
  output [31:0] t0_Value,
  output [31:0] t1_Value,
  output [31:0] t2_Value,
  output [31:0] t3_Value,
  output [31:0] Read_Data_1,
  output [31:0] Read_Data_2
);

  wire demultiplexer_1_out0, demultiplexer_1_out1, demultiplexer_1_out2, demultiplexer_1_out3;
  wire [31:0] demultiplexer_2_out0, demultiplexer_2_out1, demultiplexer_2_out2, demultiplexer_2_out3,
       multiplexer_3_out, multiplexer_4_out, multiplexer_5_out, multiplexer_6_out;

  Multiplexer #(.select(2), .width(32)) multiplexer_1 (
    .in0(t0_Value), .in1(t1_Value), .in2(t2_Value), .in3(t3_Value), .out(Read_Data_2), .sel(Read_register_2));  // open: en
  Demultiplexer #(.select(2)) demultiplexer_1 (
    .out0(demultiplexer_1_out0), .out1(demultiplexer_1_out1), .out2(demultiplexer_1_out2),
    .out3(demultiplexer_1_out3), .in(RegWrite), .sel(write_register));  // open: en
  Multiplexer #(.select(2), .width(32)) multiplexer_2 (
    .in0(t0_Value), .in1(t1_Value), .in2(t2_Value), .in3(t3_Value), .out(Read_Data_1), .sel(Read_register_1));  // open: en
  Demultiplexer #(.select(2), .width(32)) demultiplexer_2 (
    .out0(demultiplexer_2_out0), .out1(demultiplexer_2_out1), .out2(demultiplexer_2_out2),
    .out3(demultiplexer_2_out3), .in(write_data), .sel(write_register));  // open: en
  Multiplexer #(.width(32)) multiplexer_3 (
    .in0(t0_Value), .in1(demultiplexer_2_out0), .out(multiplexer_3_out), .sel(demultiplexer_1_out0));  // open: en
  Register #(.width(32)) REG_0 (.D(multiplexer_3_out), .Q(t0_Value), .clk(clock));  // open: en, clr
  Multiplexer #(.width(32)) multiplexer_4 (
    .in0(t1_Value), .in1(demultiplexer_2_out1), .out(multiplexer_4_out), .sel(demultiplexer_1_out1));  // open: en
  Register #(.width(32)) REG_1 (.D(multiplexer_4_out), .Q(t1_Value), .clk(clock));  // open: en, clr
  Multiplexer #(.width(32)) multiplexer_5 (
    .in0(t2_Value), .in1(demultiplexer_2_out2), .out(multiplexer_5_out), .sel(demultiplexer_1_out2));  // open: en
  Register #(.width(32)) REG_2 (.D(multiplexer_5_out), .Q(t2_Value), .clk(clock));  // open: en, clr
  Multiplexer #(.width(32)) multiplexer_6 (
    .in0(t3_Value), .in1(demultiplexer_2_out3), .out(multiplexer_6_out), .sel(demultiplexer_1_out3));  // open: en
  Register #(.width(32)) REG_3 (.D(multiplexer_6_out), .Q(t3_Value), .clk(clock));  // open: en, clr

  // Notes on the sheet:
  //   These are INPUTS to the circuit
  //   These are INPUTS to the circuit
  //   DO NOT CHANGE THE LOCATIONS OF THE INPUTS/OUTPUTS! IF YOU DO SO, YOU NEED TO MAKE SURE THE PINS ARE AT THE RIGHT PLACE!
  //   These are OUTPUTS to the circuit
  //   Yet again, the clock is not an actual clock, but an input, one that will be driven from a higher circuit
  //   These are OUTPUTS to the circuit
endmodule
