// Logisim project alu.circ as structural Verilog: 1 circuit, main circuit main
module main (
  input  [31:0] X,
  input  [31:0] Y,
  input  [5:0] Switch__S,
  output Signed_Overflow,
  output [31:0] RESULT,
  output Equal
);

  wire comparator_1_lt, comparator_2_lt, comparator_4_eq, comparator_5_eq, comparator_6_eq, comparator_10_eq,
       multiplexer_1_out, multiplexer_2_out, multiplexer_3_out, multiplexer_4_out, not_1_out, not_2_out,
       not_3_out, Signed_Overflow_1, Signed_Overflow_2, tagAdd, tagSub, xor_1_out, xor_2_out, xor_3_out;
  wire [4:0] bit_extender_1_out, bit_extender_2_out, bit_extender_3_out;
  wire [31:0] add, addu, \and , bit_extender_7_out, bitpal, lfsr, \or , shifter_4_out, shifter_5_out, sll,
       slt, sltu, sra, srl, sub, subu;

  Bit_Extender #(.in_width(32), .out_width(5)) bit_extender_1 (.in(Y), .out(bit_extender_1_out));
  Bit_Extender #(.in_width(32), .out_width(5)) bit_extender_2 (.in(Y), .out(bit_extender_2_out));
  Bit_Extender #(.in_width(32), .out_width(5)) bit_extender_3 (.in(Y), .out(bit_extender_3_out));
  assign \and  = X & Y;  // AND_Gate and_1, 32 bits wide
  assign \or  = X | Y;  // OR_Gate or_1, 32 bits wide
  Comparator #(.width(32)) comparator_1 (.a(X), .b(Y), .lt(comparator_1_lt));  // open: gt, eq
  Comparator #(.width(32), .mode("unsigned")) comparator_2 (.a(X), .b(Y), .lt(comparator_2_lt));  // open: gt, eq
  Comparator #(.width(32), .mode("unsigned")) comparator_3 (.a(X), .b(Y), .eq(Equal));  // open: gt, lt
  Adder #(.width(32)) adder_1 (.a(X), .b(Y), .out(addu));  // open: cin, cout
  Shifter #(.width(32)) shifter_1 (.in(X), .\dist (bit_extender_1_out), .out(sll));
  Shifter #(.width(32), .shift("lr")) shifter_2 (.in(X), .\dist (bit_extender_2_out), .out(srl));
  Shifter #(.width(32), .shift("ar")) shifter_3 (.in(X), .\dist (bit_extender_3_out), .out(sra));
  assign slt = {{31{1'b0}}, comparator_1_lt};  // Bit_Extender bit_extender_4
  assign sltu = {{31{1'b0}}, comparator_2_lt};  // Bit_Extender bit_extender_5
  xor xor_1 (xor_1_out, X[2], X[0]);
  Adder #(.width(32)) adder_2 (.a(X), .b(Y), .out(addu));  // open: cin, cout
  not not_1 (not_1_out, Y[31]);
  xor xor_2 (xor_2_out, xor_1_out, X[3]);
  Comparator #(.width(1)) comparator_4 (.a(Y[31]), .b(X[31]), .eq(comparator_4_eq));  // open: gt, lt
  Comparator #(.width(1)) comparator_5 (.a(not_1_out), .b(X[31]), .eq(comparator_5_eq));  // open: gt, lt
  Subtractor #(.width(32)) subtractor_1 (.a(X), .b(Y), .out(sub));  // open: bin, bout
  Comparator #(.width(16), .mode("unsigned")) comparator_6 (
    .a({X[0], X[1], X[2], X[3], X[4], X[5], X[6], X[7], X[8], X[9], X[10], X[11], X[12], X[13], X[14], X[15]}),
    .b(X[31:16]), .eq(comparator_6_eq));  // open: gt, lt
  Shifter #(.width(32), .shift("lr")) shifter_4 (.in(X), .\dist (5'b00001), .out(shifter_4_out));
  Multiplexer multiplexer_1 (.in0(1'b0), .in1(Signed_Overflow_1), .out(multiplexer_1_out), .sel(tagAdd));  // open: en
  Adder #(.width(32)) adder_3 (.a(X), .b(Y), .out(add));  // open: cin, cout
  Subtractor #(.width(32)) subtractor_2 (.a(X), .b(Y), .out(subu));  // open: bin, bout
  Multiplexer multiplexer_2 (.in0(not_3_out), .in1(X[31]), .out(multiplexer_2_out), .sel(comparator_5_eq));  // open: en
  assign bitpal = {{31{1'b0}}, comparator_6_eq};  // Bit_Extender bit_extender_6
  xor xor_3 (xor_3_out, xor_2_out, X[5]);
  Multiplexer multiplexer_3 (.in0(add[31]), .in1(X[31]), .out(multiplexer_3_out), .sel(comparator_4_eq));  // open: en
  not not_2 (not_2_out, add[31]);
  assign bit_extender_7_out = {{31{1'b0}}, xor_3_out};  // Bit_Extender bit_extender_7
  Multiplexer multiplexer_4 (.in0(1'b0), .in1(Signed_Overflow_2), .out(multiplexer_4_out), .sel(tagSub));  // open: en
  or or_2 (Signed_Overflow, multiplexer_4_out, multiplexer_1_out);
  Multiplexer #(.select(5), .width(32)) multiplexer_5 (
    .in0(sll), .in2(srl), .in3(sra), .in16(add), .in17(addu), .in18(sub), .in19(subu), .in20(\and ),
    .in21(\or ), .in26(slt), .in27(sltu), .in30(bitpal), .in31(lfsr), .out(RESULT),
    .sel({Switch__S[5], Switch__S[3:0]}));  // open: in1, in4, in5, in6, in7, in8, in9, in10, in11, in12, in13, in14, in15, in22, in23, in24, in25, in28, in29, en
  Comparator #(.width(5), .mode("unsigned")) comparator_7 (
    .a({Switch__S[5], Switch__S[3:0]}), .b(5'b10010), .eq(tagSub));  // open: gt, lt
  Shifter #(.width(32), .shift("rr")) shifter_5 (.in(bit_extender_7_out), .\dist (5'b00001), .out(shifter_5_out));
  Comparator #(.width(1)) comparator_8 (.a(multiplexer_3_out), .b(not_2_out), .eq(Signed_Overflow_1));  // open: gt, lt
  Comparator #(.width(5), .mode("unsigned")) comparator_9 (
    .a({Switch__S[5], Switch__S[3:0]}), .b(5'b10000), .eq(tagAdd));  // open: gt, lt
  not not_3 (not_3_out, sub[31]);
  Comparator #(.width(1)) comparator_10 (.a(multiplexer_2_out), .b(sub[31]), .eq(comparator_10_eq));  // open: gt, lt
  assign lfsr = shifter_4_out | shifter_5_out;  // OR_Gate or_3, 32 bits wide
  not not_4 (Signed_Overflow_2, comparator_10_eq);

  // Other names for the same wires on the sheet: Input_X[31:0] = X; Input_Y[31:0] = Y; isEq = Equal;
  //   control[4:0] = {Switch__S[5], Switch__S[3:0]}

  // Notes on the sheet:
  //   INPUTS to your circuit
  //   INPUT to your circuit
  //   Shift Left Logical
  //   Shift Right Logical
  //   Shift Right Arithmetic
  //   and
  //   or
  //   slt
  //   sltu
  //   signed
  //   bitpal
  //   lfsr
  //   addu
  //   DON'T CHANGE THE INPUTS AND OUTPUTS! IF YOU DO SO, YOU NEED TO MAKE SURE THE PINS ARE IN THE RIGHT PLACES!
  //   subu
  //   add
  //   OUTPUTS of your circuit
  //   sub
endmodule
