// Logisim project cpu.circ as structural Verilog: 3 circuits, main circuit main
module main (
  input  [31:0] RS_READ_VALUE,
  input  [31:0] RT_READ_VALUE,
  input  [31:0] INSTRUCTION,
  input  CLOCK,
  input  RESET,
  output [31:0] t0,
  output [31:0] t1,
  output [31:0] t2,
  output [31:0] t3,
  output [4:0] RS,
  output [4:0] RT,
  output [4:0] Write_Register,
  output [31:0] RD_WRITE_VALUE,
  output RD_WRITE_ENABLE,
  output [23:0] FETCH_ADDRESS
);

  wire access_Byte, ALU_signed_overflow, ALUSrc, amiLUI, and_1_out, and_2_out, and_3_out, comparator_1_eq,
       comparator_2_eq, comparator_3_eq, comparator_5_eq, is_BEQ, is_BNE, isBranchTaken, isEqual_ALU, isJal,
       isJR, isJump, isKill, isRsTemp, isRtTemp, isShamt, MemToReg, MemWr, not_1_out, not_2_out, not_3_out,
       or_2_out, RegDest, tempornah_2_rsout, ZeroExtend;
  wire [1:0] multiplexer_2_out;
  wire [2:0] instructType;
  wire [4:0] Write_Reg;
  wire [5:0] ALUCtr;
  wire [7:0] bit_extender_6_out;
  wire [15:0] address_j;
  wire [23:0] adder_1_out, adder_2_out, adder_3_out, bit_extender_1_out, branchVal, multiplexer_3_out,
       multiplexer_8_out, nextPC, subtractor_1_out, subtractor_2_out;
  wire [31:0] ALU_result, bit_extender_2_out, bit_extender_3_out, bit_extender_4_out, bit_extender_5_out,
       bit_extender_7_out, MEM_data_mem_out, multiplexer_7_out, multiplexer_13_out, multiplexer_15_out,
       multiplexer_16_out, multiplexer_17_out, multiplexer_18_out, multiplexer_19_out, multiplexer_20_out,
       RegFile_read_data_1, RegFile_read_data_2, rt_dataIn, subtractor_3_out, valueForBranch, Write_Data;
  wire [31:26] instruction_t;

  Register #(.width(24)) PC (.D(nextPC), .Q(FETCH_ADDRESS), .clk(CLOCK));  // open: en, clr
  and and_1 (and_1_out, is_BNE, not_1_out);
  not not_1 (not_1_out, isEqual_ALU);
  Multiplexer #(.width(5)) multiplexer_1 (
    .in0(Write_Reg), .in1({5{1'b1}}), .out(Write_Register), .sel(isJal));  // open: en
  Control control_1 (
    .instruction({instruction_t, RS, RT, address_j}), .RegDest(RegDest), .ALUCtr(ALUCtr),
    .regWrite(RD_WRITE_ENABLE), .isJal(isJal), .ALUSrc(ALUSrc), .amiLUI(amiLUI), .MemWr(MemWr),
    .MemToReg(MemToReg), .ZeroExtend(ZeroExtend), .is_BEQ(is_BEQ), .is_BNE(is_BNE),
    .access_Byte(access_Byte), .isJR(isJR), .isJump(isJump), .isShamt(isShamt));
  tempOrNah tempornah_1 (.rs(RS), .rt(RT), .rsOut(isRsTemp), .rtOut(isRtTemp));
  and and_2 (and_2_out, isEqual_ALU, is_BEQ);
  Subtractor #(.width(24)) subtractor_1 (
    .a({RS[2:0], RT, address_j}), .b(24'h100000), .out(subtractor_1_out));  // open: bin, bout
  Multiplexer #(.width(2)) multiplexer_2 (
    .in0(RT[1:0]), .in1(address_j[12:11]), .out(multiplexer_2_out), .sel(RegDest));  // open: en
  Multiplexer #(.width(24)) multiplexer_3 (
    .in0(branchVal), .in1(subtractor_1_out), .out(multiplexer_3_out), .sel(isJump));  // open: en
  Multiplexer #(.width(32)) multiplexer_4 (
    .in0(Write_Data), .in1(bit_extender_2_out), .out(RD_WRITE_VALUE), .sel(isJal));  // open: en
  and and_3 (and_3_out, RD_WRITE_ENABLE, tempornah_2_rsout);
  Multiplexer #(.width(5)) multiplexer_5 (
    .in0(RT), .in1(address_j[15:11]), .out(Write_Reg), .sel(RegDest));  // open: en
  or or_1 (isBranchTaken, and_1_out, and_2_out);
  Multiplexer #(.width(24)) multiplexer_6 (
    .in0(multiplexer_3_out), .in1(subtractor_2_out), .out(nextPC), .sel(isJR));  // open: en
  Subtractor #(.width(24)) subtractor_2 (
    .a(valueForBranch[23:0]), .b(24'h100000), .out(subtractor_2_out));  // open: bin, bout
  Register #(.width(32)) Pipeline (
    .D(multiplexer_7_out), .Q({instruction_t, RS, RT, address_j}), .clk(CLOCK));  // open: en, clr
  Multiplexer #(.width(32)) multiplexer_7 (
    .in0(INSTRUCTION), .in1({32{1'b0}}), .out(multiplexer_7_out), .sel(isKill));  // open: en
  regfile_main RegFile (
    .Read_register_1(RS[1:0]), .Read_register_2(RT[1:0]), .write_register(multiplexer_2_out),
    .write_data(Write_Data), .t0_Value(t0), .t1_Value(t1), .t2_Value(t2), .t3_Value(t3),
    .RegWrite(and_3_out), .clock(CLOCK), .Read_Data_1(RegFile_read_data_1), .Read_Data_2(RegFile_read_data_2));
  tempOrNah tempornah_2 (.rs(Write_Reg), .rsOut(tempornah_2_rsout));  // open: rt, rtOut
  Multiplexer #(.width(24)) multiplexer_8 (
    .in0(adder_1_out), .in1(FETCH_ADDRESS), .out(multiplexer_8_out), .sel(isKill));  // open: en
  Adder #(.width(24)) adder_1 (.a(FETCH_ADDRESS), .b(24'h1), .out(adder_1_out));  // open: cin, cout
  assign bit_extender_1_out = {{8{address_j[15]}}, address_j};  // Bit_Extender bit_extender_1
  Multiplexer #(.width(24)) multiplexer_9 (
    .in0(multiplexer_8_out), .in1(adder_3_out), .out(branchVal), .sel(isBranchTaken));  // open: en
  Adder #(.width(24)) adder_2 (.a(FETCH_ADDRESS), .b(24'h1), .out(adder_2_out));  // open: cin, cout
  Comparator #(.width(6)) comparator_1 (.a({6{1'b0}}), .b(instruction_t), .eq(comparator_1_eq));  // open: gt, lt
  Comparator #(.width(6)) comparator_2 (.a(instruction_t), .b(6'b000010), .eq(comparator_2_eq));  // open: gt, lt
  Comparator #(.width(6)) comparator_3 (.a(instruction_t), .b(6'b000011), .eq(comparator_3_eq));  // open: gt, lt
  Adder #(.width(24)) adder_3 (.a(multiplexer_8_out), .b(bit_extender_1_out), .out(adder_3_out));  // open: cin, cout
  assign bit_extender_2_out = {{8{1'b0}}, adder_2_out};  // Bit_Extender bit_extender_2
  Multiplexer multiplexer_10 (.in0(1'b0), .in1(1'b1), .out(instructType[0]), .sel(comparator_1_eq));  // open: en
  or or_2 (or_2_out, comparator_2_eq, comparator_3_eq);
  Multiplexer #(.width(32)) multiplexer_11 (
    .in0(RS_READ_VALUE), .in1(RegFile_read_data_1), .out(valueForBranch), .sel(isRsTemp));  // open: en
  Multiplexer #(.width(32)) multiplexer_12 (
    .in0(RT_READ_VALUE), .in1(RegFile_read_data_2), .out(rt_dataIn), .sel(isRtTemp));  // open: en
  assign bit_extender_3_out = {{16{address_j[15]}}, address_j};  // Bit_Extender bit_extender_3
  Multiplexer #(.width(32)) multiplexer_13 (
    .in0(bit_extender_3_out), .in1(bit_extender_4_out), .out(multiplexer_13_out), .sel(ZeroExtend));  // open: en
  assign bit_extender_4_out = {{16{1'b0}}, address_j};  // Bit_Extender bit_extender_4
  Subtractor #(.width(32)) subtractor_3 (.a(valueForBranch), .b(rt_dataIn), .out(subtractor_3_out));  // open: bin, bout
  Multiplexer multiplexer_14 (.in0(1'b0), .in1(1'b1), .out(instructType[1]), .sel(or_2_out));  // open: en
  or or_3 (isKill, isJump, isBranchTaken);
  not not_2 (not_2_out, instructType[0]);
  not not_3 (not_3_out, instructType[1]);
  Multiplexer #(.width(32)) multiplexer_15 (
    .in0(rt_dataIn), .in1(multiplexer_13_out), .out(multiplexer_15_out), .sel(ALUSrc));  // open: en
  and and_4 (instructType[2], not_2_out, not_3_out);
  Multiplexer #(.width(32)) multiplexer_16 (
    .in0(valueForBranch), .in1(multiplexer_15_out), .out(multiplexer_16_out), .sel(amiLUI));  // open: en
  Comparator #(.width(32)) comparator_4 (.a(subtractor_3_out), .b({32{1'b0}}), .eq(isEqual_ALU));  // open: gt, lt
  Multiplexer #(.width(32)) multiplexer_17 (
    .in0(multiplexer_15_out), .in1(32'h10), .out(multiplexer_17_out), .sel(amiLUI));  // open: en
  assign bit_extender_5_out = {{27{1'b0}}, address_j[10:6]};  // Bit_Extender bit_extender_5
  Multiplexer #(.width(32)) multiplexer_18 (
    .in0(multiplexer_16_out), .in1(rt_dataIn), .out(multiplexer_18_out), .sel(isShamt));  // open: en
  alu_main ALU (
    .Switch__S(ALUCtr), .X(multiplexer_18_out), .RESULT(ALU_result), .Signed_Overflow(ALU_signed_overflow),
    .Y(multiplexer_19_out));  // open: Equal
  Multiplexer #(.width(32)) multiplexer_19 (
    .in0(multiplexer_17_out), .in1(bit_extender_5_out), .out(multiplexer_19_out), .sel(isShamt));  // open: en
  LED led_1 (.in(ALU_signed_overflow));
  mem_main MEM (
    .Data_Mem_Addr(ALU_result), .Data_Mem_In(rt_dataIn), .ACCESS_BYTE(access_Byte), .MEM_WRITE(MemWr),
    .CLOCK(CLOCK), .Data_Mem_Out(MEM_data_mem_out));
  Bit_Extender #(.in_width(32), .out_width(8)) bit_extender_6 (.in(MEM_data_mem_out), .out(bit_extender_6_out));
  assign bit_extender_7_out = {{24{bit_extender_6_out[7]}}, bit_extender_6_out};  // Bit_Extender bit_extender_7
  Comparator #(.width(6)) comparator_5 (.a(instruction_t), .b(6'b100000), .eq(comparator_5_eq));  // open: gt, lt
  Multiplexer #(.width(32)) multiplexer_20 (
    .in0(MEM_data_mem_out), .in1(bit_extender_7_out), .out(multiplexer_20_out), .sel(comparator_5_eq));  // open: en
  Multiplexer #(.width(32)) multiplexer_21 (
    .in0(ALU_result), .in1(multiplexer_20_out), .out(Write_Data), .sel(MemToReg));  // open: en

  // Other names for the same wires on the sheet: funct[5:0] = address_j[5:0]; immediate[15:0] = address_j;
  //   instruction_t[25:0] = {RS, RT, address_j}; shamt[4:0] = address_j[10:6]; rd[4:0] = address_j[15:11];
  //   address_j[25:16] = {RS, RT}; opcode[5:0] = instruction_t; PC[23:0] = FETCH_ADDRESS; RegWr = RD_WRITE_ENABLE

  // Notes on the sheet:
  //   Put incremented pc address here for next instruction
  //   These are outputs/inputs from run.circ
  //   Decode
  //   Feel free to move these components
  //   SHOULD WE SIGN OR ZERO EXTEND THIS VALUE
  //   These are outputs to run.circ
  //   Determining the Instruction Type
endmodule

module tempOrNah (
  input  [4:0] rs,
  input  [4:0] rt,
  output rsOut,
  output rtOut
);

  wire comparator_1_lt, comparator_2_lt, comparator_3_lt, comparator_4_lt;

  Comparator #(.width(5), .mode("unsigned")) comparator_1 (.a(5'b00111), .b(rt), .lt(comparator_1_lt));  // open: gt, eq
  Comparator #(.width(5), .mode("unsigned")) comparator_2 (.a(rt), .b(5'b01100), .lt(comparator_2_lt));  // open: gt, eq
  Comparator #(.width(5), .mode("unsigned")) comparator_3 (.a(5'b00111), .b(rs), .lt(comparator_3_lt));  // open: gt, eq
  Comparator #(.width(5), .mode("unsigned")) comparator_4 (.a(rs), .b(5'b01100), .lt(comparator_4_lt));  // open: gt, eq
  and and_1 (rsOut, comparator_3_lt, comparator_4_lt);
  and and_2 (rtOut, comparator_1_lt, comparator_2_lt);
endmodule

module Control (
  input  [31:0] instruction,
  output RegDest,
  output regWrite,
  output ALUSrc,
  output [5:0] ALUCtr,
  output amiLUI,
  output MemWr,
  output MemToReg,
  output ZeroExtend,
  output is_BEQ,
  output is_BNE,
  output access_Byte,
  output isJR,
  output isJump,
  output isJal,
  output isShamt
);

  wire and_3_out, comparator_2_eq, comparator_3_eq, comparator_4_eq, comparator_5_eq, comparator_6_eq,
       comparator_7_eq, comparator_8_eq, comparator_10_eq, comparator_11_eq, comparator_14_eq,
       comparator_15_eq, comparator_16_eq, comparator_18_eq, comparator_19_eq, comparator_20_eq,
       comparator_21_eq, comparator_22_eq, comparator_23_eq, comparator_24_eq, comparator_25_eq,
       comparator_26_eq, comparator_27_eq, comparator_28_eq, comparator_29_eq, comparator_30_eq,
       comparator_31_eq, comparator_32_eq, comparator_34_eq, comparator_35_eq, or_1_out, or_2_out, or_3_out,
       or_5_out, or_7_out;
  wire [5:0] multiplexer_2_out, multiplexer_3_out;

  Comparator #(.width(6), .mode("unsigned")) comparator_1 (
    .a(instruction[31:26]), .b({6{1'b0}}), .eq(RegDest));  // open: gt, lt
  Comparator #(.width(6)) comparator_2 (.a(instruction[31:26]), .b(6'b001101), .eq(comparator_2_eq));  // open: gt, lt
  Comparator #(.width(6)) comparator_3 (.a(instruction[31:26]), .b(6'b001100), .eq(comparator_3_eq));  // open: gt, lt
  Comparator #(.width(6)) comparator_4 (.a(instruction[5:0]), .b({6{1'b0}}), .eq(comparator_4_eq));  // open: gt, lt
  Comparator #(.width(6)) comparator_5 (.a(instruction[5:0]), .b(6'b000010), .eq(comparator_5_eq));  // open: gt, lt
  Comparator #(.width(6)) comparator_6 (.a(instruction[5:0]), .b(6'b000011), .eq(comparator_6_eq));  // open: gt, lt
  Comparator #(.width(6), .mode("unsigned")) comparator_7 (
    .a(instruction[31:26]), .b({6{1'b0}}), .eq(comparator_7_eq));  // open: gt, lt
  Comparator #(.width(6)) comparator_8 (.a(instruction[31:26]), .b({6{1'b0}}), .eq(comparator_8_eq));  // open: gt, lt
  Comparator #(.width(6)) comparator_9 (.a(instruction[31:26]), .b(6'b101011), .eq(MemWr));  // open: gt, lt
  Comparator #(.width(6)) comparator_10 (.a(instruction[31:26]), .b({6{1'b0}}), .eq(comparator_10_eq));  // open: gt, lt
  or or_1 (or_1_out, comparator_4_eq, comparator_5_eq, comparator_6_eq);
  Comparator #(.width(6), .mode("unsigned")) comparator_11 (
    .a(instruction[31:26]), .b(6'b000010), .eq(comparator_11_eq));  // open: gt, lt
  Multiplexer #(.width(6)) multiplexer_1 (
    .in0(multiplexer_2_out), .in1(instruction[5:0]), .out(ALUCtr), .sel(comparator_8_eq));  // open: en
  Comparator #(.width(6)) comparator_12 (.a(instruction[31:26]), .b(6'b000100), .eq(is_BEQ));  // open: gt, lt
  Comparator #(.width(6)) comparator_13 (.a(instruction[31:26]), .b(6'b000101), .eq(is_BNE));  // open: gt, lt
  Comparator #(.width(6)) comparator_14 (.a(instruction[31:26]), .b({6{1'b0}}), .eq(comparator_14_eq));  // open: gt, lt
  Comparator #(.width(6)) comparator_15 (.a(instruction[5:0]), .b(6'b001000), .eq(comparator_15_eq));  // open: gt, lt
  and and_1 (isShamt, comparator_10_eq, or_1_out);
  or or_2 (or_2_out, comparator_11_eq, comparator_18_eq, and_3_out, or_7_out);
  not not_1 (regWrite, or_2_out);
  or or_3 (or_3_out, comparator_7_eq, comparator_27_eq, comparator_32_eq);
  not not_2 (ALUSrc, or_3_out);
  or or_4 (ZeroExtend, comparator_2_eq, comparator_3_eq);
  and and_2 (isJR, comparator_14_eq, comparator_15_eq);
  Comparator #(.width(6)) comparator_16 (.a(instruction[31:26]), .b(6'b000010), .eq(comparator_16_eq));  // open: gt, lt
  Comparator #(.width(6)) comparator_17 (.a(instruction[31:26]), .b(6'b000011), .eq(isJal));  // open: gt, lt
  Comparator #(.width(6), .mode("unsigned")) comparator_18 (
    .a(instruction[31:26]), .b(6'b000011), .eq(comparator_18_eq));  // open: gt, lt
  Comparator #(.width(6)) comparator_19 (.a(instruction[31:26]), .b(6'b001001), .eq(comparator_19_eq));  // open: gt, lt
  Comparator #(.width(6)) comparator_20 (.a(instruction[31:26]), .b(6'b100000), .eq(comparator_20_eq));  // open: gt, lt
  Comparator #(.width(6)) comparator_21 (.a(instruction[31:26]), .b(6'b100100), .eq(comparator_21_eq));  // open: gt, lt
  Comparator #(.width(6)) comparator_22 (.a(instruction[31:26]), .b(6'b100011), .eq(comparator_22_eq));  // open: gt, lt
  Comparator #(.width(6)) comparator_23 (.a(instruction[31:26]), .b(6'b101011), .eq(comparator_23_eq));  // open: gt, lt
  Comparator #(.width(6)) comparator_24 (.a(instruction[31:26]), .b(6'b100000), .eq(comparator_24_eq));  // open: gt, lt
  Comparator #(.width(6)) comparator_25 (.a(instruction[31:26]), .b(6'b100100), .eq(comparator_25_eq));  // open: gt, lt
  Comparator #(.width(6)) comparator_26 (.a(instruction[31:26]), .b(6'b100011), .eq(comparator_26_eq));  // open: gt, lt
  Comparator #(.width(6), .mode("unsigned")) comparator_27 (
    .a(instruction[31:26]), .b(6'b000010), .eq(comparator_27_eq));  // open: gt, lt
  or or_5 (or_5_out, comparator_19_eq, comparator_20_eq, comparator_21_eq, comparator_22_eq, comparator_23_eq);
  Comparator #(.width(6)) comparator_28 (.a(instruction[31:26]), .b(6'b100000), .eq(comparator_28_eq));  // open: gt, lt
  Comparator #(.width(6)) comparator_29 (.a(instruction[31:26]), .b(6'b100100), .eq(comparator_29_eq));  // open: gt, lt
  or or_6 (isJump, comparator_16_eq, isJal);
  Comparator #(.width(6), .mode("unsigned")) comparator_30 (
    .a(instruction[31:26]), .b({6{1'b0}}), .eq(comparator_30_eq));  // open: gt, lt
  and and_3 (and_3_out, comparator_30_eq, comparator_31_eq);
  or or_7 (or_7_out, comparator_35_eq, comparator_34_eq);
  or or_8 (MemToReg, comparator_24_eq, comparator_25_eq, comparator_26_eq);
  Comparator #(.width(6), .mode("unsigned")) comparator_31 (
    .a(instruction[5:0]), .b(6'b001000), .eq(comparator_31_eq));  // open: gt, lt
  Comparator #(.width(6), .mode("unsigned")) comparator_32 (
    .a(instruction[31:26]), .b(6'b000011), .eq(comparator_32_eq));  // open: gt, lt
  Comparator #(.width(6)) comparator_33 (.a(instruction[31:26]), .b(6'b001111), .eq(amiLUI));  // open: gt, lt
  or or_9 (access_Byte, comparator_28_eq, comparator_29_eq);
  Multiplexer #(.width(6)) multiplexer_2 (
    .in0(multiplexer_3_out), .in1(6'b100001), .out(multiplexer_2_out), .sel(or_5_out));  // open: en
  Multiplexer #(.width(6)) multiplexer_3 (
    .in0(6'b100101), .in1({6{1'b0}}), .out(multiplexer_3_out), .sel(amiLUI));  // open: en
  Comparator #(.width(6), .mode("unsigned")) comparator_34 (
    .a(instruction[31:26]), .b(6'b000101), .eq(comparator_34_eq));  // open: gt, lt
  Comparator #(.width(6), .mode("unsigned")) comparator_35 (
    .a(instruction[31:26]), .b(6'b000100), .eq(comparator_35_eq));  // open: gt, lt

  // Other names for the same wires on the sheet: address_j[25:0] = instruction[25:0]; funct[5:0] = instruction[5:0];
  //   immediate[15:0] = instruction[15:0]; shamt[4:0] = instruction[10:6]; rd[4:0] = instruction[15:11];
  //   rt[4:0] = instruction[20:16]; rs[4:0] = instruction[25:21]; opcode[5:0] = instruction[31:26]
endmodule
