// Logisim project mem.circ as structural Verilog: 1 circuit, main circuit main
module main (
  input  [31:0] Data_Mem_Addr,
  input  [31:0] Data_Mem_In,
  input  ACCESS_BYTE,
  input  MEM_WRITE,
  input  CLOCK,
  output [31:0] Data_Mem_Out
);

  wire not_1_out;
  wire [1:0] SaveByte;
  wire [7:0] multiplexer_1_out;
  wire [31:0] ByteData, Data;
  wire [31:2] subtractor_1_out;

  Subtractor #(.width(32)) subtractor_1 (
    .a(Data_Mem_Addr), .b(32'h10010000), .out({subtractor_1_out, SaveByte}));  // open: bin, bout
  RAM #(.addrWidth(24), .dataWidth(32), .bus("separate")) ram_1 (
    .addr(subtractor_1_out[25:2]), .din(Data_Mem_In), .data(Data), .str(MEM_WRITE), .clk(CLOCK),
    .ld(not_1_out));  // open: sel, clr
  not not_1 (not_1_out, MEM_WRITE);
  Multiplexer #(.select(2), .width(8), .enable("false")) multiplexer_1 (
    .in0(Data[31:24]), .in1(Data[23:16]), .in2(Data[15:8]), .in3(Data[7:0]), .out(multiplexer_1_out),
    .sel(SaveByte));
  assign ByteData = {{24{1'b0}}, multiplexer_1_out};  // Bit_Extender bit_extender_1
  Multiplexer #(.width(32), .enable("false")) multiplexer_2 (
    .in0(Data), .in1(ByteData), .out(Data_Mem_Out), .sel(ACCESS_BYTE));

  // Other names for the same wires on the sheet: clk = CLOCK; output[31:0] = Data_Mem_Out

  // Notes on the sheet:
  //   These are INPUTS to the circuit
  //   These are INPUTS to the circuit
  //   DO NOT CHANGE THE LOCATIONS OF THE INPUTS/OUTPUTS! IF YOU DO SO, YOU NEED TO MAKE SURE THE PINS ARE AT THE RIGHT PLACE!
  //   Yet again, the clock is not an actual clock, but an input, one that will be driven from a higher circuit
  //   This is an OUTPUT to the circuit
endmodule
